// Digital circuit Escada_Rolante.dig as structural Verilog
module Escada_Rolante (
  input  clk,
  input  clk_2,
  input  clk_3
);

  wire and_1_out, and_2_out, and_3_out, and_4_out, and_5_out, and_6_out, and_7_out, and_8_out, and_9_out,
       and_10_out, and_11_out, and_12_out, and_13_out, and_14_out, and_15_out, and_16_out, and_17_out,
       and_18_out, and_19_out, and_20_out, and_21_out, and_22_out, and_23_out, and_24_out, jk_ff_1_q,
       jk_ff_2_q, jk_ff_3_q, jk_ff_4_nq, jk_ff_5_q, jk_ff_6_q, jk_ff_7_q, jk_ff_8_q, not_1_out, not_2_out,
       not_3_out, not_4_out, not_5_out, not_6_out, not_7_out, not_8_out, not_9_out, not_10_out, not_11_out,
       not_12_out, not_13_out, not_14_out, not_15_out, or_1_out, or_2_out, or_3_out, or_4_out, or_5_out,
       or_6_out, or_7_out, or_8_out, or_9_out, or_10_out, or_11_out, or_12_out, or_13_out, or_14_out,
       or_15_out, or_16_out, or_17_out, or_18_out, or_19_out, or_20_out, or_21_out, S1_out, S2_out,
       t_ff_1_nq, t_ff_1_q, t_ff_2_nq, t_ff_2_q, t_ff_3_nq, t_ff_3_q, t_ff_4_nq, t_ff_4_q;

  Button S1 (.out(S1_out));
  JK_FF jk_ff_1 (.J(1'b1), .C(S1_out), .K(1'b1), .Q(jk_ff_1_q));  // open: nQ
  not not_1 (not_1_out, jk_ff_1_q);
  Button S2 (.out(S2_out));
  T_FF t_ff_1 (.T(1'b1), .C(S2_out), .Q(t_ff_1_q), .nQ(t_ff_1_nq));
  and and_1 (and_1_out, not_1_out, t_ff_1_q);
  and and_2 (and_2_out, jk_ff_1_q, t_ff_1_nq);
  or or_1 (or_1_out, and_1_out, and_2_out);
  T_FF t_ff_2 (.T(1'b1), .C(or_1_out), .Q(t_ff_2_q), .nQ(t_ff_2_nq));
  and and_3 (and_3_out, not_1_out, t_ff_2_q);
  and and_4 (and_4_out, jk_ff_1_q, t_ff_2_nq);
  or or_2 (or_2_out, and_3_out, and_4_out);
  T_FF t_ff_3 (.T(1'b1), .C(or_2_out), .Q(t_ff_3_q), .nQ(t_ff_3_nq));
  and and_5 (and_5_out, not_1_out, t_ff_3_q);
  and and_6 (and_6_out, jk_ff_1_q, t_ff_3_nq);
  or or_3 (or_3_out, and_5_out, and_6_out);
  T_FF t_ff_4 (.T(1'b1), .C(or_3_out), .Q(t_ff_4_q), .nQ(t_ff_4_nq));
  and and_7 (and_7_out, not_1_out, t_ff_4_q);
  and and_8 (and_8_out, jk_ff_1_q, t_ff_4_nq);
  or or_4 (or_4_out, and_7_out, and_8_out);
  not not_2 (not_2_out, or_1_out);
  not not_3 (not_3_out, or_4_out);
  not not_4 (not_4_out, or_3_out);
  not not_5 (not_5_out, or_2_out);
  and and_9 (and_9_out, not_5_out, not_4_out, not_3_out, not_2_out);
  and and_10 (and_10_out, not_5_out, not_4_out, or_1_out);
  and and_11 (and_11_out, not_4_out, or_2_out, not_2_out);
  and and_12 (and_12_out, or_2_out, or_2_out, or_1_out);
  and and_13 (and_13_out, not_5_out, or_3_out, not_2_out, not_3_out);
  and and_14 (and_14_out, or_1_out, or_3_out, not_3_out);
  and and_15 (and_15_out, or_3_out, not_2_out, or_2_out);
  and and_16 (and_16_out, and_13_out, jk_ff_3_q);
  or or_5 (or_5_out, and_16_out, and_9_out);
  JK_FF jk_ff_2 (.J(and_14_out), .C(clk_2), .K(or_5_out), .Q(jk_ff_2_q));  // open: nQ
  LED Lv (.in(jk_ff_2_q));
  or or_6 (or_6_out, and_9_out, and_12_out, and_15_out, and_11_out, and_14_out);
  or or_7 (or_7_out, and_10_out, and_11_out, and_13_out, and_9_out, and_12_out);
  or or_8 (or_8_out, and_9_out, and_12_out, and_10_out, and_14_out, and_13_out);
  or or_9 (or_9_out, and_11_out, and_11_out, and_12_out, and_9_out, and_14_out);
  or or_10 (or_10_out, and_9_out, and_15_out, and_11_out);
  or or_11 (or_11_out, and_9_out, and_14_out, and_13_out, and_15_out);
  or or_12 (or_12_out, and_11_out, and_13_out, and_15_out, and_12_out, and_14_out);
  or or_13 (or_13_out, and_15_out, 1'b0);
  or or_14 (or_14_out, and_15_out, 1'b0);
  or or_15 (or_15_out, jk_ff_2_q, and_9_out, and_15_out);
  not not_6 (not_6_out, jk_ff_2_q);
  and and_17 (and_17_out, or_15_out, and_15_out);
  Seven_Seg seven_seg_1 (
    .a(or_6_out), .b(or_7_out), .c(or_17_out), .d(or_18_out), .e(or_10_out), .f(or_11_out), .g(or_12_out),
    .dp(1'b1));
  or or_16 (or_16_out, and_17_out, and_9_out);
  or or_17 (or_17_out, or_8_out, or_14_out);
  and and_18 (and_18_out, and_10_out, not_6_out);
  or or_18 (or_18_out, or_9_out, or_13_out);
  JK_FF jk_ff_3 (.J(and_18_out), .C(clk_3), .K(or_16_out), .Q(jk_ff_3_q));  // open: nQ
  LED M (.in(jk_ff_3_q));
  or or_19 (or_19_out, or_3_out, or_1_out, or_2_out, or_4_out);
  not not_7 (not_7_out, jk_ff_3_q);
  not not_8 (not_8_out, or_19_out);
  and and_19 (and_19_out, not_7_out, and_24_out);
  and and_20 (and_20_out, not_8_out, clk);
  JK_FF jk_ff_4 (.J(1'b1), .C(and_19_out), .K(1'b1), .nQ(jk_ff_4_nq));  // open: Q
  JK_FF jk_ff_5 (.J(1'b1), .C(and_21_out), .K(1'b1), .Q(jk_ff_5_q));  // open: nQ
  and and_21 (and_21_out, and_20_out, jk_ff_4_nq);
  JK_FF jk_ff_6 (.J(1'b1), .C(jk_ff_5_q), .K(1'b1), .Q(jk_ff_6_q));  // open: nQ
  JK_FF jk_ff_7 (.J(1'b1), .C(jk_ff_6_q), .K(1'b1), .Q(jk_ff_7_q));  // open: nQ
  not not_9 (not_9_out, jk_ff_7_q);
  not not_10 (not_10_out, jk_ff_8_q);
  not not_11 (not_11_out, not_10_out);
  not not_12 (not_12_out, jk_ff_5_q);
  not not_13 (not_13_out, jk_ff_6_q);
  not not_14 (not_14_out, not_9_out);
  not not_15 (not_15_out, not_13_out);
  JK_FF jk_ff_8 (.J(1'b1), .C(jk_ff_7_q), .K(1'b1), .Q(jk_ff_8_q));  // open: nQ
  and and_22 (and_22_out, not_14_out, not_15_out);
  or or_20 (or_20_out, not_11_out, and_22_out);
  or or_21 (or_21_out, jk_ff_3_q, and_23_out);
  LED M_2 (.in(or_21_out));
  and and_23 (and_23_out, or_20_out, or_20_out);
  and and_24 (and_24_out, not_12_out, not_13_out, not_9_out, not_10_out);

  // Notes on the sheet:
  //   BCD 7 SEGMENTOS
  //   A
  //   B
  //   C
  //   D
  //   E
  //   F
  //   G
endmodule
